// Logisim project maquina de estado.circ as structural Verilog: 1 circuit, main circuit main
module main (
  input  s1,
  input  s0,
  input  lig,
  input  c,
  input  cont,
  output out,
  output en,
  output clr,
  output n1,
  output n0
);

  wire and_4_out, and_5_out, and_6_out, and_7_out, and_8_out, and_9_out, and_10_out, not_1_out, not_2_out,
       not_3_out, not_4_out, not_5_out, not_6_out, not_7_out, not_8_out, not_9_out, not_10_out, not_11_out,
       not_12_out, not_13_out, not_14_out, not_15_out, not_16_out, not_17_out;

  not not_1 (not_1_out, s1);
  not not_2 (not_2_out, s0);
  not not_3 (not_3_out, s1);
  not not_4 (not_4_out, s0);
  not not_5 (not_5_out, c);
  not not_6 (not_6_out, cont);
  not not_7 (not_7_out, s0);
  not not_8 (not_8_out, cont);
  not not_9 (not_9_out, c);
  not not_10 (not_10_out, s1);
  not not_11 (not_11_out, s0);
  not not_12 (not_12_out, s1);
  not not_13 (not_13_out, c);
  not not_14 (not_14_out, s0);
  not not_15 (not_15_out, cont);
  not not_16 (not_16_out, lig);
  not not_17 (not_17_out, c);
  and and_1 (out, not_1_out, s0);
  and and_2 (en, s1, not_2_out);
  and and_3 (clr, not_3_out, not_4_out);
  and and_4 (and_4_out, s0, lig, not_5_out, not_6_out);
  and and_5 (and_5_out, s1, not_7_out, not_8_out);
  and and_6 (and_6_out, s1, s0, not_9_out);
  and and_7 (and_7_out, not_10_out, not_11_out);
  and and_8 (and_8_out, not_12_out, not_13_out, cont);
  and and_9 (and_9_out, not_14_out, c, not_15_out);
  and and_10 (and_10_out, s0, not_16_out, not_17_out);
  or or_1 (n1, and_4_out, and_5_out, and_6_out);
  or or_2 (n0, and_7_out, and_8_out, and_9_out, and_10_out);
endmodule
